# Fritzing sketch Stick_Jump_Circuit (saved by Fritzing 0.9.3b)
circuit board: 8.46667cm x 5.64444cm
breadboards: 3

parts:
  LCD1 = LCD screen
  Part1 = Arduino Uno (Rev3)
  Disp1 = LBT2088AH [part_number=LBT2088AH]
  U1 = MAX7219 [package=dil24]
  R6 = Resistor [tolerance=±5% resistance=100k package="0603 [SMD]"]
  C2 = Electrolytic Capacitor [capacitance=10μF package="0605 [SMD, electrolytic]"]
  C3 = Ceramic Capacitor [capacitance="100 nF" package="0603 [SMD, multilayer]"]
  S1 = Pushbutton [package="[SMD]"]
  S2 = Pushbutton [package="[SMD]"]
  R8 = Resistor [tolerance=±5% resistance=10k package="0805 [SMD]"]
  R7 = Resistor [tolerance=±5% resistance=220 package=THT]
  R9 = Resistor [tolerance=±5% resistance=10k package="0805 [SMD]"]

nets:
  GND: LCD1.VSS, LCD1.R/W, LCD1.LED-, Part1.GND, U1.GND, U1.GND2, C2.-, C3.0, R8.Pin_1, R9.Pin_0
  VDD: LCD1.VDD, Part1.5V, U1.VCC, R6.Pin_0, C2.+, C3.1, S1.Pin_1, S1.Pin_2, S2.Pin_1, S2.Pin_2, R7.Pin_1
  N1: LCD1.V0, Part1.D9_PWM
  N2: LCD1.RS, Part1.D3_PWM
  N3: LCD1.E, Part1.D4
  N4: LCD1.DB4, Part1.D5_PWM
  N5: LCD1.DB5, Part1.D6_PWM
  N6: LCD1.DB6, Part1.D7
  N7: LCD1.DB7, Part1.D8
  N8: LCD1.LED+, R7.Pin_0
  N9: Part1.D10_PWM/SS, U1.LOAD
  N10: Part1.D11_PWM/MOSI, U1.CLK
  N11: Part1.D12/MISO, U1.DIN
  N12: Part1.D13/SCK, S2.Pin_3, S2.Pin_4, R9.Pin_1
  N13: Part1.D2, S1.Pin_3, S1.Pin_4, R8.Pin_0
  N14: Disp1.pin1, U1.DIG4
  N15: Disp1.pin2, U1.DIG6
  N16: Disp1.pin_3, U1.SEGA
  N17: Disp1.pin_4, U1.SEGB
  N18: Disp1.pin_5, U1.DIG7
  N19: Disp1.pin_6, U1.SEGD
  N20: Disp1.pin_7, U1.DIG5
  N21: Disp1.pin_8, U1.DIG2
  N22: Disp1.pin_9, U1.DIG0
  N23: Disp1.pin_10, U1.SEGC
  N24: Disp1.pin_11, U1.SEGE
  N25: Disp1.pin_12, U1.DIG3
  N26: Disp1.pin_13, U1.SEGDP
  N27: Disp1.pin_14, U1.DIG1
  N28: Disp1.pin_15, U1.SEGF
  N29: Disp1.pin_16, U1.SEGG
  N30: U1.ISET, R6.Pin_1

notes:
  100kΩ
  220Ω
  10μF
  100 nF
  10kΩ
